# Fritzing sketch dht11eli (1) (saved by Fritzing 0.9.3b)
circuit board: 6.88566cm x 5.36311cm
breadboards: 1

parts:
  R2 = Resistor [tolerance=±5% resistance=220 package=THT]
  Arduino1 = Arduino Uno (Rev3)
  DHT1 = DHT11 Humitidy and Temperature Sensor  # not connected
  R3 = Resistor [tolerance=±5% resistance=220 package=THT]

nets (from the breadboard view):
  N1: R2.Pin_0, Arduino1.D9_PWM, Arduino1.5V, R3.Pin_0

custom parts:
  DHT11 Humitidy and Temperature Sensor: DHT11 Humidity and Temperature Sensor

// code stored in the sketch: Untitled3.ino
#include <SimpleDHT.h>

int pinDHT11 = 5; // el pin donde envio datos 
SimpleDHT11 dht11(pinDHT11);

void setup() {
  Serial.begin(115200);
  
}

void loop() {
  // start working...
  Serial.println("====hola=======");
  Serial.println("Sample DHT11...");
  
  // read without samples.
  byte temperature = 0;
  byte humidity = 0;
  int err = SimpleDHTErrSuccess;
  if ((err = dht11.read(&temperature, &humidity, NULL)) != SimpleDHTErrSuccess) {
    Serial.println("Read DHT11 failed, err="); 
    Serial.println(err);delay(1000);
    return;
    delay(1000);
  }
  
  Serial.println("Sample OK: ");
  Serial.println((int)temperature); Serial.println(" *C, ");
   
  Serial.println((int)humidity); Serial.println(" H");
  
  // DHT11 sampling rate is 1HZ.
  delay(1500);
}
